# Fritzing sketch Schematic (saved by Fritzing 0.9.3b)
breadboards: 1

parts:
  Raspberry_Pi_1 = Raspberry Pi 3 [part_number=RPI-3-V1.2]
  LED1 = smd LED [color="White (4500K)" package="0603 [SMD]"]
  LED2 = smd LED [color="Green (565nm)" package="0603 [SMD]"]
  LED3 = smd LED [color="Blue (430nm)" package="0603 [SMD]"]
  R1 = Resistor [tolerance=±5% resistance=220 package="2010 [SMD]"]
  R2 = Resistor [tolerance=±5% resistance=220 package="2010 [SMD]"]
  R3 = Resistor [tolerance=±5% resistance=220 package="2010 [SMD]"]

nets:
  N1: Raspberry_Pi_1.GIPO17, R2.Pin_1
  N2: Raspberry_Pi_1.GIPO27, R1.Pin_1
  N3: Raspberry_Pi_1.GIPO18, R3.Pin_1
  N4: Raspberry_Pi_1.GND, LED1.cathode, LED2.cathode, LED3.cathode
  N5: LED1.anode, R1.Pin_0
  N6: LED2.anode, R2.Pin_0
  N7: LED3.anode, R3.Pin_0
